# Fritzing sketch wheelchair project 2 (saved by Fritzing 0.8.7b)
breadboards: 2

parts:
  Part1 = Arduino Mega 2560 (Rev3)
  D1 = LTE-302 [package=lte-302]
  D2 = LTE-302 [package=lte-302]
  D3 = LTE-302 [package=lte-302]
  S1 = SPST Switch [package=switch-spst-smd-a]
  GY2 = MPU-6050 Board GY-521 [form="♀ (female)" package=THT]

nets:
  N1: Part1.D21/SCL, GY2.pin3
  N2: Part1.D20/SDA, GY2.pin4
  N3: Part1.5V, GY2.pin1
  N4: Part1.GND, D1.C, D2.C, D3.C, GY2.pin2
  N5: Part1.D2_PWM, S1.O
  N6: Part1.D7_PWM, D3.A
  N7: Part1.D25, D1.A
  N8: D2.A, S1.P

notes:
  front sensor: trig on digital pin 8
  echo on digital pin 9
  front left sensor: trig on digital pin 12
  echo on digital pin 13
  front right sensor: trig on digital pin 23
  echo on digital pin 22
  back sensor: trig on digital pin 8
  echo on digital pin 9
  back left sensor: trig on digital pin 52
  echo on digital pin 53
  back right sensor: trig on digital pin 50
  echo on digital pin 51
  led left: digital pin 7
  led right: digital pin 25
  led center (vibrator) : 2
  Mpu-6050:VCC to 5v pin of arduino
  Mpu-6050:Gnd to Gnd pin of arduino
  Mpu-6050:SCL to SCL pin of arduino
  Mpu-6050:SDA to SDA pin of arduino
  Vin or Vcc: 5V
  power to sensors: pin 48 of arduino

custom parts:
  MPU-6050 Board GY-521: Acelerometro y Giroscopio MPU-6050 Board GY-521
